# Fritzing sketch Leonardo_schematics_starter_led_handbrake (saved by Fritzing 0.9.3b)
breadboards: 1

parts:
  Part1 = Arduino Leonardo (Rev3b)
  U1 = ENCODER-QUADRATURE [package=encoder-16mm-quad]
  LED1 = LED - 5mm [color="Red (633nm)" package="5 mm [THT]"]
  LED2 = LED - 5mm [color="Orange (612nm)" package="5 mm [THT]"]
  M1 = DC Motor
  R1 = Resistor [tolerance=±5% resistance=220 package="0402 [SMD]"]
  R2 = Resistor [tolerance=±5% resistance=220 package="0402 [SMD]"]

nets:
  N1: Part1.D1/TX, M1.pin_2
  N2: Part1.D2/SDA, M1.pin_1
  N3: Part1.5V, U1.A
  N4: Part1.GND, U1.C, LED1.cathode, LED2.cathode
  N5: Part1.A0, U1.B
  N6: Part1.D12/A11, R2.Pin_0
  N7: Part1.D13_PWM, R1.Pin_0

notes:
  Ignitionbox
  Left pin : starter
  Middle: battery (5v)
  Right: ignition
