# Fritzing sketch UNO_schematics (saved by Fritzing 0.9.3b)
breadboards: 1

parts:
  Part1 = Arduino Uno (Rev3)
  U1 = ENCODER-QUADRATURE [package=encoder-16mm-quad]
  J1 = JST-VHR-3N [part_number=JST-VHR-3N package=THT]

nets:
  N1: Part1.A0, U1.B
  N2: Part1.5V, U1.A, J1.pin_5
  N3: Part1.GND, U1.C

notes:
  Did not find a schematic for a Ignitionbox, but
  Pins are;
  Left: Starter
  Middle: Battery ( 5v )
  Right: Ignition
  Ignitionbox
